# Fritzing sketch DCSscheme (saved by Fritzing 0.9.3b)
breadboards: 1

parts:
  Load = DC Motor
  ArduinoDue = Arduino Due (Rev2b)
  U1 = L298_BRIDGE_DRIVER [package=powerso20]
  Motor+Encoder = DC Motor with two-phase hall-encoder [part_number=VT-E-G25A-06-177E]
  IC1 = LM324 [package=dil16]
  R1 = Resistor [tolerance=±5% resistance=1 package="0805 [SMD]"]
  R2 = Resistor [tolerance=±5% resistance=33k package="0805 [SMD]"]
  R3 = Resistor [tolerance=±5% resistance=33k package="0805 [SMD]"]
  R4 = Resistor [tolerance=±5% resistance=12k package="1206 [SMD]"]
  R5 = Resistor [tolerance=±5% resistance=12k package="1206 [SMD]"]
  Potentiometer = Rotary Potentiometer (Small) [maximum_resistance=1kΩ package=THT]
  V1 = DC Power [voltage=12V frequency=60]

nets:
  N1: Load.pin_1, U1.OUT3
  N2: Load.pin_2, U1.OUT4
  N3: ArduinoDue.A0, Potentiometer.wiper
  N4: ArduinoDue.A1, IC1.OUT1, R3.Pin_1
  N5: ArduinoDue.5V, Motor+Encoder.pin2, R4.Pin_0, R5.Pin_0, Potentiometer.leg2
  N6: ArduinoDue.GND, Motor+Encoder.pin5
  N7: ArduinoDue.D8_PWM, Motor+Encoder.pin4, R4.Pin_1
  N8: ArduinoDue.D10_PWM/SS0, Motor+Encoder.pin3, R5.Pin_1
  N9: ArduinoDue.D2_PWM, U1.ENA
  N10: ArduinoDue.D3_PWM, U1.IN1
  N11: ArduinoDue.D4_PWM/SS1, U1.IN2
  N12: ArduinoDue.D5_PWM, U1.IN3
  N13: ArduinoDue.D6_PWM, U1.IN4
  N14: ArduinoDue.D7_PWM, U1.ENB
  N15: U1.SENSE_A, IC1.IN1+, R1.Pin_1
  N16: U1.OUT1, Motor+Encoder.pin6
  N17: U1.OUT2, Motor+Encoder.pin1
  GND: U1.GND, IC1.GND, V1.V-
  N18: U1.VSS, IC1.V+, V1.V+
  N19: IC1.IN1-, R2.Pin_0, R3.Pin_0
  GND_2: R1.Pin_0, R2.Pin_1, Potentiometer.leg1

custom parts:
  LM324: LM324 Quad OpAmp
